// Logisim project BCDadder.circ as structural Verilog: 1 circuit, main circuit main
module main (
);

  wire n7408_1_pin3, n7408_1_pin6, n7432_1_pin3, n74283_1_pin1, n74283_1_pin2, n74283_1_pin3, n74283_1_pin4,
       n74283_1_pin5, n74283_1_pin6, n74283_1_pin8, n74283_1_pin9, n74283_1_pin10, n74283_1_pin11,
       n74283_1_pin12, n74283_1_pin13, n74283_1_pin14, n74283_1_pin15, n74283_2_pin1, n74283_2_pin2,
       n74283_2_pin4, n74283_2_pin9, n74283_2_pin10, n74283_2_pin13, switch_1_p1, switch_1_p2;

  // Switch switch_1: pin names not known; wires that end beside it: switch_1_p1, switch_1_p2
  _74283 #(.VccGndPorts("true")) u_74283_1 (
    .pin1(n74283_1_pin1), .pin2(n74283_1_pin2), .pin3(n74283_1_pin3), .pin4(n74283_1_pin4),
    .pin5(n74283_1_pin5), .pin6(n74283_1_pin6), .pin7(switch_1_p2), .pin8(n74283_1_pin8),
    .pin16(switch_1_p1), .pin15(n74283_1_pin15), .pin14(n74283_1_pin14), .pin13(n74283_1_pin13),
    .pin12(n74283_1_pin12), .pin11(n74283_1_pin11), .pin10(n74283_1_pin10), .pin9(n74283_1_pin9));
  _7408 #(.VccGndPorts("true")) u_7408_1 (
    .pin1(n74283_1_pin13), .pin2(n74283_1_pin10), .pin3(n7408_1_pin3), .pin4(n74283_1_pin1),
    .pin5(n74283_1_pin10), .pin6(n7408_1_pin6), .pin7(n74283_1_pin8), .pin14(switch_1_p1));  // open: pin13, pin12, pin11, pin10, pin9, pin8
  // Switch switch_2: pin names not known; wires that end beside it: n74283_1_pin12
  // Switch switch_3: pin names not known; wires that end beside it: n74283_1_pin14
  // Switch switch_4: pin names not known; wires that end beside it: switch_1_p1, n74283_1_pin11, switch_1_p1
  // Switch switch_5: pin names not known; wires that end beside it: n74283_1_pin15, switch_1_p1
  // Switch switch_6: pin names not known; wires that end beside it: n74283_1_pin3
  // Switch switch_7: pin names not known; wires that end beside it: n74283_1_pin5
  // Switch switch_8: pin names not known; wires that end beside it: n74283_1_pin2, switch_1_p1
  // Switch switch_9: pin names not known; wires that end beside it: n74283_1_pin6
  LED led_1 (.in(n74283_2_pin9));
  _74283 #(.VccGndPorts("true")) u_74283_2 (
    .pin1(n74283_2_pin1), .pin2(n74283_2_pin2), .pin3(n74283_1_pin1), .pin4(n74283_2_pin4),
    .pin5(n74283_1_pin4), .pin6(n74283_1_pin8), .pin7(n74283_1_pin8), .pin8(n74283_1_pin8),
    .pin16(switch_1_p1), .pin15(n74283_2_pin2), .pin14(n74283_1_pin13), .pin13(n74283_2_pin13),
    .pin12(n74283_1_pin10), .pin11(n74283_1_pin8), .pin10(n74283_2_pin10), .pin9(n74283_2_pin9));
  _7432 #(.VccGndPorts("true")) u_7432_1 (
    .pin1(n7408_1_pin6), .pin2(n7408_1_pin3), .pin3(n7432_1_pin3), .pin4(n7432_1_pin3), .pin5(n74283_1_pin9),
    .pin6(n74283_2_pin2), .pin7(n74283_1_pin8), .pin14(switch_1_p1));  // open: pin13, pin12, pin11, pin10, pin9, pin8
  LED led_2 (.in(n74283_2_pin10));
  LED led_3 (.in(n74283_2_pin13));
  LED led_4 (.in(n74283_2_pin1));
  LED led_5 (.in(n74283_2_pin4));
  // also tied to GND on the sheet: n74283_1_pin8
  // also tied to VCC on the sheet: switch_1_p1
endmodule
