// Logisim project SR_flipflop.circ as structural Verilog: 1 circuit, main circuit main
module main (
  input  in_1,
  input  in_2
);

  wire clock_1_out, n7400_1_pin1, n7400_1_pin2, n7400_1_pin3, n7400_1_pin5;

  Clock clock_1 (.out(clock_1_out));
  _7400 u_7400_1 (
    .pin1(n7400_1_pin1), .pin2(n7400_1_pin2), .pin3(n7400_1_pin3), .pin4(n7400_1_pin3), .pin5(n7400_1_pin5),
    .pin6(n7400_1_pin1), .pin13(in_2), .pin12(clock_1_out), .pin11(n7400_1_pin2), .pin10(clock_1_out),
    .pin9(in_1), .pin8(n7400_1_pin5));
  LED led_1 (.in(n7400_1_pin3));
  LED led_2 (.in(n7400_1_pin1));
endmodule
