// Logisim project UNIVERSAL_GATE.circ as structural Verilog: 1 circuit, main circuit main
module main (
  input  in_1,
  input  in_2,
  input  in_3,
  input  in_4,
  input  in_5,
  input  in_6,
  input  in_7,
  input  in_8,
  input  in_9,
  input  in_10,
  input  in_11
);

  wire nand_1_out, nand_2_out, nand_3_out, nand_4_out, nand_5_out, nand_6_out, nor_1_out, nor_2_out,
       nor_3_out, nor_4_out, nor_5_out, nor_6_out;

  nand nand_1 (nand_1_out, in_2, in_4);
  nand nand_2 (nand_2_out, in_6, in_6);
  LED led_1 (.in(nand_2_out));
  nor nor_1 (nor_1_out, in_8, in_8);
  LED led_2 (.in(nor_1_out));
  nor nor_2 (nor_2_out, in_10, in_10);
  nor nor_3 (nor_3_out, in_11, in_11);
  nand nand_3 (nand_3_out, nand_1_out, nand_1_out);
  LED led_3 (.in(nand_3_out));
  nor nor_4 (nor_4_out, nor_2_out, nor_3_out);
  LED led_4 (.in(nor_4_out));
  nor nor_5 (nor_5_out, in_7, in_9);
  nand nand_4 (nand_4_out, in_3, in_3);
  nand nand_5 (nand_5_out, in_5, in_5);
  nor nor_6 (nor_6_out, nor_5_out, nor_5_out);
  nand nand_6 (nand_6_out, nand_4_out, nand_5_out);
  LED led_5 (.in(nor_6_out));
  LED led_6 (.in(nand_6_out));

  // Notes on the sheet:
  //   AND
  //   NOT
  //   NOT
  //   AND
  //   OR
  //   OR
endmodule
