// Logisim project UNIVERSAL_TO_XOR.circ as structural Verilog: 1 circuit, main circuit main
module main (
  input  in_1,
  input  in_2,
  input  in_3,
  input  in_4,
  input  in_5,
  input  A,
  input  in_7,
  input  N,
  input  in_9,
  input  in_10,
  input  in_11,
  input  in_12,
  input  in_13,
  input  in_14,
  input  in_15,
  input  in_16,
  input  in_17,
  input  in_18,
  input  in_19,
  input  in_20
);

  wire n7400_1_pin1, n7400_1_pin3, n7400_1_pin5, n7400_1_pin6, n7402_1_pin1, n7402_1_pin3, n7402_1_pin4,
       n7402_1_pin5, nand_1_out, nand_2_out, nand_3_out, nand_4_out, nand_5_out, nand_6_out, nand_7_out,
       nand_8_out, nand_9_out, nand_10_out, nor_1_out, nor_2_out, nor_3_out, nor_4_out, nor_5_out, nor_6_out,
       nor_7_out, nor_8_out, nor_9_out, nor_10_out, nor_11_out, nor_12_out;

  nand nand_1 (nand_1_out, in_3, in_4);
  nand nand_2 (nand_2_out, in_7, in_7);
  nor nor_1 (nor_1_out, in_14, in_16);
  _7400 u_7400_1 (
    .pin1(n7400_1_pin1), .pin2(in_19), .pin3(n7400_1_pin3), .pin4(n7400_1_pin3), .pin5(n7400_1_pin5),
    .pin6(n7400_1_pin6), .pin13(in_19), .pin12(in_17), .pin11(n7400_1_pin1), .pin10(n7400_1_pin1),
    .pin9(in_17), .pin8(n7400_1_pin5));
  LED led_1 (.in(nand_2_out));
  nor nor_2 (nor_2_out, in_10, in_12);
  nor nor_3 (nor_3_out, in_14, nor_1_out);
  nor nor_4 (nor_4_out, nor_1_out, in_16);
  nand nand_3 (nand_3_out, nand_1_out, nand_1_out);
  LED led_2 (.in(nand_3_out));
  nor nor_5 (nor_5_out, nor_2_out, nor_2_out);
  LED led_3 (.in(nor_5_out));
  nor nor_6 (nor_6_out, nor_3_out, nor_4_out);
  LED led_4 (.in(n7400_1_pin6));
  nor nor_7 (nor_7_out, nor_6_out, nor_6_out);
  LED led_5 (.in(nor_7_out));
  _7402 u_7402_1 (
    .pin1(n7402_1_pin1), .pin2(in_20), .pin3(n7402_1_pin3), .pin4(n7402_1_pin4), .pin5(n7402_1_pin5),
    .pin6(n7402_1_pin1), .pin13(n7402_1_pin5), .pin12(in_18), .pin11(n7402_1_pin3), .pin10(n7402_1_pin3),
    .pin9(in_18), .pin8(in_20));
  nand nand_4 (nand_4_out, A, N);
  nand nand_5 (nand_5_out, in_2, in_2);
  nand nand_6 (nand_6_out, in_5, in_5);
  nand nand_7 (nand_7_out, A, nand_4_out);
  nand nand_8 (nand_8_out, nand_4_out, N);
  nor nor_8 (nor_8_out, in_11, in_11);
  nor nor_9 (nor_9_out, in_13, in_13);
  nor nor_10 (nor_10_out, in_15, in_15);
  nand nand_9 (nand_9_out, nand_5_out, nand_6_out);
  nor nor_11 (nor_11_out, nor_8_out, nor_9_out);
  LED led_6 (.in(nor_11_out));
  LED led_7 (.in(nor_10_out));
  LED led_8 (.in(nor_12_out));
  nor nor_12 (nor_12_out, n7402_1_pin4, n7402_1_pin4);
  LED led_9 (.in(nand_9_out));
  nand nand_10 (nand_10_out, nand_7_out, nand_8_out);
  LED led_10 (.in(nand_10_out));

  // Notes on the sheet:
  //   AND
  //   NOT
  //   NOR
  //   OR
  //   NAND TO XOR
  //   N
  //   D
  //   XOR
  //   AND
  //   NOT
  //   NOR TO XOR
  //   OR
  //   NOT
endmodule
