// Logisim project all_flipflop.circ as structural Verilog: 1 circuit, main circuit main
module main (
  input  S,
  input  R,
  input  J,
  input  K,
  input  R_2,
  input  S_2
);

  wire and_1_out, and_2_out, and_3_out, and_4_out, clock_1_out, clock_2_out, clock_3_out, nand_1_out,
       nand_2_out, nand_3_out, nand_4_out, nor_1_out, nor_2_out, nor_3_out, nor_4_out;

  Clock clock_1 (.out(clock_1_out));
  Clock clock_2 (.out(clock_2_out));
  Clock clock_3 (.out(clock_3_out));
  and and_1 (and_1_out, S, clock_1_out);
  and and_2 (and_2_out, clock_1_out, R);
  and and_3 (and_3_out, nor_3_out, J, clock_2_out);
  and and_4 (and_4_out, clock_2_out, K, nor_4_out);
  nand nand_1 (nand_1_out, R_2, clock_3_out);
  nand nand_2 (nand_2_out, clock_3_out, S_2);
  nor nor_1 (nor_1_out, and_1_out, nor_2_out);
  nor nor_2 (nor_2_out, nor_1_out, and_2_out);
  nor nor_3 (nor_3_out, and_3_out, nor_3_out);
  nor nor_4 (nor_4_out, nor_4_out, and_4_out);
  nand nand_3 (nand_3_out, nand_1_out, nand_4_out);
  nand nand_4 (nand_4_out, nand_3_out, nand_2_out);
  LED led_1 (.in(nor_1_out));
  LED led_2 (.in(nor_2_out));
  LED led_3 (.in(nor_3_out));
  LED led_4 (.in(nor_4_out));
  LED led_5 (.in(nand_3_out));
  LED led_6 (.in(nand_4_out));

  // Notes on the sheet:
  //   CLK
  //   CLK
  //   SR flip Flop
  //   JK flipflop
  //   RS flip Flop
  //   Q
  //   Q'
  //   Q
  //   Q'
  //   Q
  //   Q'
endmodule
