// Logisim project flip_flop.circ as structural Verilog: 1 circuit, main circuit main
module main (
  input  S,
  input  J,
  input  R,
  input  K,
  input  D,
  input  T
);

  wire clock_1_out, clock_2_out, clock_3_out, clock_4_out, nand_1_out, nand_2_out, nand_3_out, nand_4_out,
       nand_5_out, nand_6_out, nand_7_out, nand_8_out, nand_9_out, nand_10_out, nand_11_out, nand_12_out,
       nand_13_out, nand_14_out, nor_1_out, nor_2_out, not_1_out;

  Clock clock_1 (.out(clock_1_out));
  Clock clock_2 (.out(clock_2_out));
  Clock clock_3 (.out(clock_3_out));
  not not_1 (not_1_out, D);
  nand nand_1 (nand_1_out, S, clock_1_out);
  nand nand_2 (nand_2_out, clock_1_out, R);
  nand nand_3 (nand_3_out, D, clock_2_out);
  nand nand_4 (nand_4_out, clock_2_out, not_1_out);
  nand nand_5 (nand_5_out, nor_1_out, T, clock_3_out);
  nand nand_6 (nand_6_out, clock_3_out, T, nor_2_out);
  nand nand_7 (nand_7_out, nand_1_out, nand_8_out);
  nand nand_8 (nand_8_out, nand_7_out, nand_2_out);
  nand nand_9 (nand_9_out, nand_3_out, nand_10_out);
  nand nand_10 (nand_10_out, nand_9_out, nand_4_out);
  nor nor_1 (nor_1_out, nand_5_out, nor_2_out);
  nor nor_2 (nor_2_out, nor_1_out, nand_6_out);
  LED led_1 (.in(nand_7_out));
  LED led_2 (.in(nand_8_out));
  LED led_3 (.in(nor_1_out));
  LED led_4 (.in(nor_2_out));
  LED led_5 (.in(nand_9_out));
  LED led_6 (.in(nand_10_out));
  Clock clock_4 (.out(clock_4_out));
  nand nand_11 (nand_11_out, nand_13_out, J, clock_4_out);
  nand nand_12 (nand_12_out, clock_4_out, K, nand_14_out);
  nand nand_13 (nand_13_out, nand_11_out, nand_14_out);
  nand nand_14 (nand_14_out, nand_13_out, nand_12_out);
  LED led_7 (.in(nand_13_out));
  LED led_8 (.in(nand_14_out));

  // Notes on the sheet:
  //   clk
  //   clk
  //   clk
  //   D Flip Flop
  //   SR Flip Flop
  //   T Flip Flop
  //   Q
  //   Q'
  //   Q
  //   Q'
  //   Q
  //   Q'
  //   clk
  //   JK Flip_Flop
  //   Q
  //   Q'
endmodule
