// Logisim project sr_by_nand.circ as structural Verilog: 1 circuit, main circuit main
module main (
  input  in_1,
  input  in_2
);

  wire clock_1_out, n7400_1_pin3, n7400_1_pin5, n7400_1_pin6, n7400_1_pin11;

  Clock clock_1 (.out(clock_1_out));
  _7400 u_7400_1 (
    .pin1(clock_1_out), .pin2(in_2), .pin3(n7400_1_pin3), .pin4(n7400_1_pin3), .pin5(n7400_1_pin5),
    .pin6(n7400_1_pin6), .pin13(clock_1_out), .pin12(in_1), .pin11(n7400_1_pin11), .pin10(n7400_1_pin11),
    .pin9(n7400_1_pin6), .pin8(n7400_1_pin5));
  LED led_1 (.in(n7400_1_pin5));
  LED led_2 (.in(n7400_1_pin6));
endmodule
